# Fritzing sketch ArduinoMusic (saved by Fritzing 0.9.3b)

parts:
  LED5 = LED - 5mm [color="White (4500K)" package="5 mm [THT]"]
  LED7 = LED - 5mm [color="White (4500K)" package="5 mm [THT]"]
  LED8 = LED - 5mm [color="White (4500K)" package="5 mm [THT]"]
  LED9 = LED - 5mm [color="White (4500K)" package="5 mm [THT]"]
  LED10 = LED - 5mm [color="White (4500K)" package="5 mm [THT]"]
  LED11 = LED - 5mm [color="White (4500K)" package="5 mm [THT]"]
  LED12 = LED - 5mm [color="White (4500K)" package="5 mm [THT]"]
  SP1 = SPEAKER [package=pcb_mount_speaker]
  Pro_Micro1 = Pro Micro

nets:
  N1: LED5.cathode, LED7.cathode, LED8.cathode, LED9.cathode, LED10.cathode, LED11.cathode, LED12.cathode, SP1.+, Pro_Micro1.GND
  N2: LED5.anode, Pro_Micro1.D7
  N3: LED7.anode, Pro_Micro1.D6
  N4: LED8.anode, Pro_Micro1.D8
  N5: LED9.anode, Pro_Micro1.D3
  N6: LED10.anode, Pro_Micro1.D5
  N7: LED11.anode, Pro_Micro1.D2
  N8: LED12.anode, Pro_Micro1.D4
  N9: SP1.-, Pro_Micro1.D10

custom parts:
  Pro Micro: The SparkFun Pro Micro is a complete USB-based microcontoller development system, in a very small footprint, capable of implementing many types of projects. All programming can be done via the USB port.
